# Fritzing sketch circuit (saved by Fritzing 0.9.3b)

parts:
  HC-SR04_Sensor_1 = HC-SR04 Ultrasonic Distance Sensor
  Part2 = Bluetooth HC-05 Macho
  U2 = LIPO-2000mAh [package=lipo-2000]
  U3 = Vibration Motor- ROB-08449 [package=vibe-motor-10mm]
  IC1 = L293D [package=THT]
  Part3 = Power Cell LiPo Charger/Booster
  USB_A = USB Connectors [package=usb-minib]
  USB_MINI-B = USB Connectors [package=usb-a-h]
  S1 = SWITCH-MOMENTARY-2 [package=tactile-switch-1101ne]
  S2 = SWITCH-MOMENTARY-2 [package=tactile_switch_smd-2]
  S3 = SWITCH-MOMENTARY-2 [package=tactile_switch_smd-2]
  S4 = SWITCH-MOMENTARY-2 [package=tactile_switch_smd-2]
  S5 = SWITCH-MOMENTARY-2 [package=tactile_switch_smd-2]
  R1 = Resistor [tolerance=±5% resistance=220 package="0402 [SMD]"]
  R2 = Resistor [tolerance=±5% resistance=220 package="0402 [SMD]"]
  R3 = Resistor [tolerance=±5% resistance=220 package="0402 [SMD]"]
  R4 = Resistor [tolerance=±5% resistance=220 package="0402 [SMD]"]
  U1 = Vibration Motor- ROB-08449 [package=vibe-motor-10mm]
  LED1 = smd LED [color="Red (633nm)" package="0603 [SMD]"]
  S6 = SWITCH-MOMENTARY-2 [package=tactile_switch_smd-2]
  R5 = Resistor [tolerance=±5% resistance=220 package="0402 [SMD]"]
  Part1 = Arduino Nano (Rev3.0) (ICSP)
  LED2 = smd LED [color="Green (555nm)" package="0603 [SMD]"]
  LED3 = smd LED [color="Red (633nm)" package="0603 [SMD]"]
  SP1 = SPEAKER [package=pcb_mount_speaker]

nets:
  VCC: HC-SR04_Sensor_1.VCC, Part2.VCC, IC1.Enable_1, IC1.+V, S4.1, Part1.5V
  N1: HC-SR04_Sensor_1.TRIG, Part1.D7
  GND: HC-SR04_Sensor_1.ECHO, Part2.GND, U2.-, U3.-, IC1.0V, Part3.GND, USB_A.GND, USB_MINI-B.GND, R1.Pin_1, R2.Pin_1, R3.Pin_1, R4.Pin_1, U1.-, LED1.cathode, R5.Pin_1, Part1.GND, LED2.cathode, LED3.cathode, SP1.-
  N2: HC-SR04_Sensor_1.GND, Part1.D8
  N3: Part2.State, Part1.D2
  N4: Part2.TXD, Part1.D3
  N5: Part2.RXD, Part1.D4
  N6: U2.+, Part3.VBATT, Part1.A0
  N7: U3.+, IC1.Out_2_(_Controlled_by_Enable_1_)
  N8: IC1.In_1, IC1.In_2, Part1.D5
  N9: IC1.Out_1_(_Controlled_by_Enable_1_), U1.+
  N10: Part3.VCC, USB_A.D+, S1.1
  N11: Part3.5VIN, USB_MINI-B.D+
  N12: S1.2, Part1.VIN
  N13: S2.2, R3.Pin_0, Part1.D10
  N14: S2.1, S3.1, S5.1, LED2.anode
  N15: S3.2, R2.Pin_0, Part1.D6
  N16: S4.2, R1.Pin_0, Part1.D9
  N17: S5.2, R4.Pin_0
  N18: LED1.anode, Part1.A7
  N19: S6.2, R5.Pin_0
  N20: Part1.A1, LED3.anode
